# Fritzing sketch NeoClock-Hardware-bb (saved by Fritzing 0.9.3b)
circuit board: 8.46667cm x 5.64444cm
breadboards: 3

parts:
  Bare-ESP-12F1 = Bare-ESP-12F
  Part1 = FTDI Basic Programmer
  FTDI = male pin header, 6 pins [form="♂ (male)"]
  PRG = Pushbutton [package="[THT]"]
  to_pixels = male pin header, 3 pins [form="♂ (male)"]
  U1 = V_REG_LD1117VXX [package=78xxl]
  RST = Pushbutton [package="[THT]"]
  Pwr_Sel = female pin header, 3 pins [form="♀ (female)"]
  5v = Power Jack [package=power_jack_pth]
  C1 = Tantalum Capacitor [capacitance=10µF voltage=20V package="100 mil [THT, tantalum]"]
  C2 = Tantalum Capacitor [capacitance=10µF voltage=20V package="100 mil [THT, tantalum]"]

nets:
  N1: Bare-ESP-12F1.REST, RST.Pin_1, RST.Pin_2
  N2: Bare-ESP-12F1.CH_PD, Bare-ESP-12F1.VCC, Bare-ESP-12F1.GPIO2, Part1.POWER, FTDI.pin4, Pwr_Sel.pin1, Pwr_Sel.pin2
  N3: Bare-ESP-12F1.GPIO14, to_pixels.pin2
  GND: Bare-ESP-12F1.GND, Bare-ESP-12F1.GPIO15, Part1.GND, FTDI.pin6, PRG.Pin_3, PRG.Pin_4, to_pixels.pin3, U1.GND, RST.Pin_3, RST.Pin_4, 5v.GND, C1.-, C2.-
  N4: Bare-ESP-12F1.GPIO0, PRG.Pin_1, PRG.Pin_2
  N5: Bare-ESP-12F1.RXD, Part1.RXI, FTDI.pin2
  N6: Bare-ESP-12F1.TXD, Part1.TXO, FTDI.pin3
  N7: to_pixels.pin1, U1.IN, 5v.PWR, C1.+
  N8: U1.OUT, Pwr_Sel.pin3, C2.+

custom parts:
  Bare-ESP-12F: ESP-12F with minimal breakout board for breadboard use. PCB uses bare ESP-12F.
